// Logisim project TFlipflop.circ as structural Verilog: 1 circuit, main circuit main
module main (
  input  in_1,
  input  in_2,
  output out_3,
  output out_4
);

  wire and_1_out, and_2_out;

  and and_1 (and_1_out, out_3, in_1, in_2);
  and and_2 (and_2_out, in_2, in_1, in_1);
  nor nor_1 (out_3, and_1_out, in_1);
  nor nor_2 (in_1, out_3, and_2_out);

  assign out_4 = in_1;

  // Notes on the sheet:
  //   T flipflop
  //   SR Flip FLop
endmodule
